# Fritzing sketch diagram (saved by Fritzing 0.9.3b)
breadboards: 1

parts:
  Part1 = Arduino Uno (Rev3)
  LED1 = LED - 5mm [color="Red (633nm)" package="5 mm [THT]"]
  LED2 = LED - 5mm [color="Green (560nm)" package="5 mm [THT]"]
  R1 = Resistor [tolerance=±5% resistance=330 package=THT]
  R2 = Resistor [tolerance=±5% resistance=330 package=THT]
  LED3 = LED - 5mm [color="Blue (470nm)" package="5 mm [THT]"]
  R3 = Resistor [tolerance=±5% resistance=330 package=THT]
  S4 = Momentary Switch [package=ksa_sealed_tac_switch]
  S5 = Momentary Switch [package=ksa_sealed_tac_switch]
  SG1 = Buzzer 12mm [package=buzzer-12mm-ns]
  U1 = BUTTON-MAGNETIC [package=Magnetic-snap]
  U2 = BUTTON-MAGNETIC [package=Magnetic-snap]  # not connected

nets:
  N1: Part1.D8, LED2.anode
  N2: Part1.D9_PWM, LED3.anode
  N3: Part1.D11_PWM/MOSI, SG1.2
  N4: Part1.GND, Part1.D2, R1.Pin_1, R2.Pin_1, R3.Pin_1, S4.1, S4.2, S5.1, S5.2, SG1.1, U1.1
  N5: Part1.D4, S4.3, S4.4
  N6: Part1.D5_PWM, S5.3, S5.4
  N7: Part1.D7, LED1.anode
  N8: LED1.cathode, R1.Pin_0
  N9: LED2.cathode, R2.Pin_0
  N10: LED3.cathode, R3.Pin_0

notes:
  magnetic switch
